// Logisim project 01_registrador_saida.circ as structural Verilog: 1 circuit, main circuit main
module main (
  input  [7:0] in_1,
  output [7:0] out_2
);

  wire button_1_out;

  Button button_1 (.out(button_1_out));
  Register register_1 (.D(in_1), .clk(button_1_out), .Q(out_2));  // open: en, clr
endmodule
