// Logisim project 03_registrador_b.circ as structural Verilog: 1 circuit, main circuit main
module main (
  input  [7:0] entrada,
  input  Ee,
  input  La,
  input  Lb,
  input  Ea,
  output [7:0] W,
  output [7:0] A_saida,
  output [7:0] B_saida
);

  wire clk;

  Button button_1 (.out(clk));
  assign W = Ee ? entrada : 8'bz;  // Controlled_Buffer controlled_buffer_1
  Register A (.D(W), .en(La), .clk(clk), .Q(A_saida));  // open: clr
  assign W = Ea ? A_saida : 8'bz;  // Controlled_Buffer controlled_buffer_2
  Register register_1 (.D(W), .en(Lb), .clk(clk), .Q(B_saida));  // open: clr
endmodule
