// Logisim project 04_somador_subtrator.circ as structural Verilog: 1 circuit, main circuit main
module main (
  input  [7:0] entrada,
  input  Ee,
  input  La,
  input  Ea,
  input  Su,
  input  Eu,
  input  Lb,
  output [7:0] W,
  output [7:0] A_saida,
  output [7:0] Soma_saida,
  output [7:0] B_saida
);

  wire clk;
  wire [7:0] multiplexer_1_out, not_1_out;

  Button button_1 (.out(clk));
  assign W = Ee ? entrada : 8'bz;  // Controlled_Buffer controlled_buffer_1
  assign W = Eu ? Soma_saida : 8'bz;  // Controlled_Buffer controlled_buffer_2
  Register A (.D(W), .en(La), .clk(clk), .Q(A_saida));  // open: clr
  assign W = Ea ? A_saida : 8'bz;  // Controlled_Buffer controlled_buffer_3
  assign not_1_out = ~B_saida;  // NOT_Gate not_1, 8 bits wide
  Register #(.trigger("falling")) B (.D(W), .en(Lb), .clk(clk), .Q(B_saida));  // open: clr
  Multiplexer #(.width(8)) multiplexer_1 (.in0(B_saida), .in1(not_1_out), .out(multiplexer_1_out), .sel(Su));
  Adder adder_1 (.a(A_saida), .b(multiplexer_1_out), .out(Soma_saida), .cin(Su));  // open: cout

  // Other names for the same wires on the sheet: Bq[7:0] = B_saida; S[7:0] = Soma_saida
endmodule
