// Logisim project 05_pc_mar_memoria.circ as structural Verilog: 1 circuit, main circuit main
module main (
  input  [7:0] entrada,
  input  Ee,
  input  La,
  input  Ea,
  input  Su,
  input  Eu,
  input  Lb,
  input  Cp,
  input  Ep,
  input  Er,
  input  Lm,
  output [7:0] W,
  output [7:0] A_saida,
  output [7:0] Soma_saida,
  output [7:0] B_saida,
  output [7:0] PC_saida,
  output [7:0] MAR_saida
);

  wire clk;
  wire [7:0] M, multiplexer_1_out, not_1_out;

  Button button_1 (.out(clk));
  Counter counter_1 (.clk(clk), .Q(PC_saida));  // open: clr, load, up, count, D, carry
  assign W = Ee ? entrada : 8'bz;  // Controlled_Buffer controlled_buffer_1
  assign W = Eu ? Soma_saida : 8'bz;  // Controlled_Buffer controlled_buffer_2
  Register A (.D(W), .en(La), .clk(clk), .Q(A_saida));  // open: clr
  assign W = Ea ? A_saida : 8'bz;  // Controlled_Buffer controlled_buffer_3
  assign not_1_out = ~B_saida;  // NOT_Gate not_1, 8 bits wide
  Register #(.trigger("falling")) B (.D(W), .en(Lb), .clk(clk), .Q(B_saida));  // open: clr
  Multiplexer #(.width(8)) multiplexer_1 (.in0(B_saida), .in1(not_1_out), .out(multiplexer_1_out), .sel(Su));
  Adder adder_1 (.a(A_saida), .b(multiplexer_1_out), .out(Soma_saida), .cin(Su));  // open: cout
  Register register_1 (.D(W), .en(Lm), .clk(clk), .Q(MAR_saida));  // open: clr
  assign W = Ep ? PC_saida : 8'bz;  // Controlled_Buffer controlled_buffer_4
  ROM rom_1 (.addr(MAR_saida), .data(M));
  assign W = Er ? M : 8'bz;  // Controlled_Buffer controlled_buffer_5

  // Other names for the same wires on the sheet: Bq[7:0] = B_saida; MAR[7:0] = MAR_saida; Pc[7:0] = PC_saida;
  //   S[7:0] = Soma_saida

  // Notes on the sheet:
  //   contents of rom_1 (hex, n*v repeats v):
  //   11 22 33 44
endmodule
